// Logisim project CPU-RCAGAMEZMATEOGUERRERO.circ as structural Verilog: 17 circuits, main circuit main
module main (
);

  wire ALUSRC, ALUSRCEX, beq, bne, CLK, debugcomponent_1_aand, debugcomponent_1_add, debugcomponent_1_addi,
       debugcomponent_1_beq, debugcomponent_1_bnq, debugcomponent_1_jump, debugcomponent_1_load,
       debugcomponent_1_none, debugcomponent_1_oor, debugcomponent_1_store, debugcomponent_1_sub,
       debugcomponent_2_aand, debugcomponent_2_add, debugcomponent_2_addi, debugcomponent_2_beq,
       debugcomponent_2_bnq, debugcomponent_2_jump, debugcomponent_2_load, debugcomponent_2_oor,
       debugcomponent_2_store, debugcomponent_2_sub, debugcomponent_3_aand, debugcomponent_3_add,
       debugcomponent_3_addi, debugcomponent_3_beq, debugcomponent_3_bnq, debugcomponent_3_jump,
       debugcomponent_3_load, debugcomponent_3_oor, debugcomponent_3_store, debugcomponent_3_sub,
       debugcomponent_4_aand, debugcomponent_4_add, debugcomponent_4_addi, debugcomponent_4_beq,
       debugcomponent_4_bnq, debugcomponent_4_jump, debugcomponent_4_load, debugcomponent_4_oor,
       debugcomponent_4_store, debugcomponent_4_sub, HAZARD, JumpCondition, MEMREGEX, MemREGMEM, MemREGWR,
       MemW, MemWEX, MemWMEM, MTR, NoneEXMem, NoneIDEX, NoneWRREG, not_1_out, not_2_out, REGDST, REGDSTEX,
       REGWRITE, REGWRITEEX, REGWRITEMEM, REGWRWR, Rst, uc_1_memread, ZERO, ZEROMem;
  wire [1:0] ALUCTRL, ALUOP, ForwardA, ForwardB, id_ex_reg_1_aluopex;
  wire [4:0] id_1_shamt, id_ex_reg_1_rsex, RD, RDEX, RS, RT, RTEX, RW, RWMem, RWWr;
  wire [5:0] FUNC, FunctEX, FunctMem, FunctWr, ifetch_1_functif, ifetch_1_opcodeif, OPCODE, OPCODEEX,
       OPCODEMem, OPCODEWr;
  wire [15:0] IMM, IMMEX;
  wire [23:0] bit_extender_1_out, bit_extender_3_out, branch_1_outvalue, Iter, PC, PcMasUno, PCmasUnoEX,
       PCmasUnoIfetch, PCmasUnoMem;
  wire [25:0] JumpAdd;
  wire [31:0] ALUData, ALUDataMem, ALUDataWr, bit_extender_2_out, BusA, BusB, BusBF, BusBMem, DataMainMemory,
       DataMemory, DataMemoryWr, InstructionIfetch, multiplexer_2_out, multiplexer_5_out, multiplexer_6_out,
       Ra, Rb;

  not not_1 (not_1_out, HAZARD);
  // Probe on not_1_out
  RAM #(.addrWidth(24), .dataWidth(32), .enables("line")) ram_1 (
    .addr(Iter), .dout(DataMainMemory));  // open: we, clk, din
  Button button_1 (.out(Rst));
  Clock clock_1 (.out(CLK));
  // Probe on CLK
  Register #(.width(24)) register_1 (.D(PC), .en(not_1_out), .Q(Iter), .clk(CLK), .clr(Rst));
  Bit_Extender #(.in_width(26), .out_width(24)) bit_extender_1 (.in(JumpAdd), .out(bit_extender_1_out));
  Branch branch_1 (.pcMasUno(PcMasUno), .IMM(IMM), .ZERO(ZERO), .beq(beq), .benq(bne), .outValue(branch_1_outvalue));
  Adder #(.width(24)) adder_1 (.a(Iter), .b(24'h1), .out(PcMasUno));  // open: cin, cout
  not not_2 (not_2_out, JumpCondition);
  // Probe on PC
  Multiplexer #(.width(24)) multiplexer_1 (
    .in0(bit_extender_1_out), .in1(branch_1_outvalue), .out(PC), .sel(not_2_out));
  UC uc_1 (
    .opcode(OPCODE), .regdst(REGDST), .regwrite(REGWRITE), .jump(JumpCondition), .bne(bne), .beq(beq),
    .alusrc(ALUSRC), .memToReg(MTR), .memRead(uc_1_memread), .memWrite(MemW), .ALU(ALUOP));
  // Probe on uc_1_memread
  // Probe on ALUOP
  // Probe on FUNC
  ID id_1 (
    .INPUTID(InstructionIfetch), .Funct(FUNC), .Shamt(id_1_shamt), .Inmediate(IMM), .RD(RD), .RT(RT),
    .RS(RS), .OPCODE(OPCODE), .JumAdd(JumpAdd));
  // Probe on id_1_shamt
  LED led_1 (.in(debugcomponent_1_addi));
  DebugComponent debugcomponent_1 (
    .opCode(ifetch_1_opcodeif), .funct(ifetch_1_functif), .Addi(debugcomponent_1_addi),
    .Load(debugcomponent_1_load), .Store(debugcomponent_1_store), .BEQ(debugcomponent_1_beq),
    .BNQ(debugcomponent_1_bnq), .Jump(debugcomponent_1_jump), .None(debugcomponent_1_none),
    .Add(debugcomponent_1_add), .Sub(debugcomponent_1_sub), .AAnd(debugcomponent_1_aand),
    .OOr(debugcomponent_1_oor));
  LED led_2 (.in(debugcomponent_1_load));
  LED led_3 (.in(debugcomponent_1_store));
  LED led_4 (.in(debugcomponent_1_beq));
  LED led_5 (.in(debugcomponent_1_bnq));
  LED led_6 (.in(debugcomponent_1_jump));
  LED led_7 (.in(debugcomponent_1_none));
  LED led_8 (.in(debugcomponent_1_add));
  LED led_9 (.in(debugcomponent_1_sub));
  LED led_10 (.in(debugcomponent_1_aand));
  LED led_11 (.in(debugcomponent_1_oor));
  // Probe on PCmasUnoIfetch
  Ifetch ifetch_1 (
    .PCmasUno(PcMasUno), .Instruction(DataMainMemory), .CLK(CLK), .RESET(Rst), .RWMesa2(RW), .RWMesa3(RWMem),
    .NoneIDEX(NoneIDEX), .NoneEXMem(NoneEXMem), .PCmasUnoResult(PCmasUnoIfetch),
    .InstructionResult(InstructionIfetch), .HAZARD(HAZARD), .FUNCTIF(ifetch_1_functif),
    .OPCODEIF(ifetch_1_opcodeif));
  // Probe on RWWr
  // Probe on RS
  // Probe on multiplexer_6_out
  // Probe on RT
  ID_EX_Reg id_ex_reg_1 (
    .PCmasUnoIfetch(PCmasUnoIfetch), .IMM(IMM), .Ra(Ra), .Rb(Rb), .RT(RT), .RD(RD), .OPCODE(OPCODE),
    .Funct(FUNC), .RESET(Rst), .CLK(CLK), .ALUOP(ALUOP), .REGDST(REGDST), .ALUSRC(ALUSRC), .MEMREG(MTR),
    .MEMWR(MemW), .REGWRITE(REGWRITE), .RS(RS), .PCmasUnoEX(PCmasUnoEX), .IMMEX(IMMEX), .BusA(BusA),
    .BusB(BusB), .RTEX(RTEX), .RDEX(RDEX), .OPCODEEX(OPCODEEX), .FunctEX(FunctEX),
    .ALUOPEX(id_ex_reg_1_aluopex), .REGDSTEX(REGDSTEX), .ALUSRCEX(ALUSRCEX), .MEMREGEX(MEMREGEX),
    .MEMWREX(MemWEX), .REGWRITEX(REGWRITEEX), .RSEX(id_ex_reg_1_rsex));
  // Probe on Ra
  UR ur_1 (
    .BUSW(multiplexer_6_out), .RESET(Rst), .RS(RS), .CLK(CLK), .RT(RT), .RW(RWWr), .REGWRITE(REGWRWR),
    .RegA(Ra), .RegB(Rb));
  // Probe on Rb
  // Probe on PCmasUnoEX
  LED led_12 (.in(debugcomponent_2_addi));
  DebugComponent debugcomponent_2 (
    .opCode(OPCODEEX), .funct(FunctEX), .Addi(debugcomponent_2_addi), .Load(debugcomponent_2_load),
    .Store(debugcomponent_2_store), .BEQ(debugcomponent_2_beq), .BNQ(debugcomponent_2_bnq),
    .Jump(debugcomponent_2_jump), .None(NoneIDEX), .Add(debugcomponent_2_add), .Sub(debugcomponent_2_sub),
    .AAnd(debugcomponent_2_aand), .OOr(debugcomponent_2_oor));
  LED led_13 (.in(debugcomponent_2_load));
  LED led_14 (.in(debugcomponent_2_store));
  LED led_15 (.in(debugcomponent_2_beq));
  LED led_16 (.in(debugcomponent_2_bnq));
  LED led_17 (.in(debugcomponent_2_jump));
  LED led_18 (.in(NoneIDEX));
  LED led_19 (.in(debugcomponent_2_add));
  LED led_20 (.in(debugcomponent_2_sub));
  LED led_21 (.in(debugcomponent_2_aand));
  LED led_22 (.in(debugcomponent_2_oor));
  // Probe on BusA
  Multiplexer #(.select(2), .width(32)) multiplexer_2 (
    .in0(BusA), .in1(multiplexer_6_out), .in2(ALUDataMem), .out(multiplexer_2_out), .sel(ForwardA));  // open: in3
  Multiplexer #(.select(2), .width(32)) multiplexer_3 (
    .in0(BusB), .in1(multiplexer_6_out), .in2(ALUDataMem), .out(BusBF), .sel(ForwardB));  // open: in3
  assign bit_extender_2_out = {{16{IMMEX[15]}}, IMMEX};  // Bit_Extender bit_extender_2
  Multiplexer #(.width(5)) multiplexer_4 (.in0(RTEX), .in1(RDEX), .out(RW), .sel(REGDSTEX));
  ForwardingUnit forwardingunit_1 (
    .RS(id_ex_reg_1_rsex), .RT(RTEX), .RWMesa3(RWMem), .RWMesa4(RWWr), .NoneEXMEM(NoneEXMem),
    .NoneMEMWR(NoneWRREG), .ForwardA(ForwardA), .ForwardB(ForwardB));
  ALU alu_1 (.ALUCTR(ALUCTRL), .BUSA(multiplexer_2_out), .BUSB(multiplexer_5_out), .Data(ALUData), .ZERO(ZERO));
  Multiplexer #(.width(32)) multiplexer_5 (
    .in0(BusBF), .in1(bit_extender_2_out), .out(multiplexer_5_out), .sel(ALUSRCEX));
  UCALU ucalu_1 (.ALUOP(id_ex_reg_1_aluopex), .FUNC(FunctEX), .OUTPUT(ALUCTRL));
  Bit_Extender #(.in_width(32), .out_width(24)) bit_extender_3 (.in(ALUDataMem), .out(bit_extender_3_out));
  RAM #(.addrWidth(24), .clearpin("true"), .dataWidth(32), .enables("line")) ram_2 (
    .addr(bit_extender_3_out), .we(MemWMEM), .clk(CLK), .din(BusBMem), .dout(DataMemory), .clr(Rst));
  // Probe on PCmasUnoMem
  EX_Mem_Reg ex_mem_reg_1 (
    .PCmasUnoEX(PCmasUnoEX), .ALUData(ALUData), .BusB(BusBF), .Zero(ZERO), .RW(RW), .OPCODE(OPCODEEX),
    .FunctEX(FunctEX), .CLK(CLK), .RESET(Rst), .MEMWR(MemWEX), .MEMREG(MEMREGEX), .REGWRITE(REGWRITEEX),
    .PCmasUnoMem(PCmasUnoMem), .OPCODEMem(OPCODEMem), .ALUDataMem(ALUDataMem), .BusBMem(BusBMem),
    .ZeroMem(ZEROMem), .RWMem(RWMem), .FunctMem(FunctMem), .MEMWREX(MemWMEM), .MEMREGMEM(MemREGMEM),
    .REGWRITEMEM(REGWRITEMEM));
  LED led_23 (.in(debugcomponent_3_addi));
  DebugComponent debugcomponent_3 (
    .opCode(OPCODEMem), .funct(FunctMem), .Addi(debugcomponent_3_addi), .Load(debugcomponent_3_load),
    .Store(debugcomponent_3_store), .BEQ(debugcomponent_3_beq), .BNQ(debugcomponent_3_bnq),
    .Jump(debugcomponent_3_jump), .None(NoneEXMem), .Add(debugcomponent_3_add), .Sub(debugcomponent_3_sub),
    .AAnd(debugcomponent_3_aand), .OOr(debugcomponent_3_oor));
  LED led_24 (.in(debugcomponent_3_load));
  LED led_25 (.in(debugcomponent_3_store));
  LED led_26 (.in(debugcomponent_3_beq));
  LED led_27 (.in(debugcomponent_3_bnq));
  LED led_28 (.in(debugcomponent_3_jump));
  LED led_29 (.in(debugcomponent_3_add));
  LED led_30 (.in(debugcomponent_3_sub));
  LED led_31 (.in(debugcomponent_3_aand));
  LED led_32 (.in(debugcomponent_3_oor));
  LED led_33 (.in(NoneEXMem));
  Mem_Wr_Reg mem_wr_reg_1 (
    .ALUDataMem(ALUDataMem), .DataMemory(DataMemory), .RWMem(RWMem), .OPCODEMem(OPCODEMem),
    .FunctMem(FunctMem), .CLK(CLK), .RESET(Rst), .MEMREG(MemREGMEM), .REGWR(REGWRITEMEM),
    .ALUDataWr(ALUDataWr), .DataMemoryWr(DataMemoryWr), .RWWr(RWWr), .OPCODEWr(OPCODEWr), .FunctWr(FunctWr),
    .MEMREGWRWR(MemREGWR), .REGWRWR(REGWRWR));
  LED led_34 (.in(debugcomponent_4_addi));
  DebugComponent debugcomponent_4 (
    .opCode(OPCODEWr), .funct(FunctWr), .Addi(debugcomponent_4_addi), .Load(debugcomponent_4_load),
    .Store(debugcomponent_4_store), .BEQ(debugcomponent_4_beq), .BNQ(debugcomponent_4_bnq),
    .Jump(debugcomponent_4_jump), .None(NoneWRREG), .Add(debugcomponent_4_add), .Sub(debugcomponent_4_sub),
    .AAnd(debugcomponent_4_aand), .OOr(debugcomponent_4_oor));
  LED led_35 (.in(debugcomponent_4_load));
  LED led_36 (.in(debugcomponent_4_store));
  LED led_37 (.in(debugcomponent_4_beq));
  LED led_38 (.in(debugcomponent_4_bnq));
  LED led_39 (.in(debugcomponent_4_jump));
  LED led_40 (.in(debugcomponent_4_add));
  LED led_41 (.in(debugcomponent_4_sub));
  LED led_42 (.in(debugcomponent_4_aand));
  LED led_43 (.in(debugcomponent_4_oor));
  LED led_44 (.in(NoneWRREG));
  Multiplexer #(.width(32)) multiplexer_6 (
    .in0(ALUDataWr), .in1(DataMemoryWr), .out(multiplexer_6_out), .sel(MemREGWR));

  // Notes on the sheet:
  //   ALU
endmodule

module ID (
  input  [31:0] INPUTID,
  output [5:0] Funct,
  output [4:0] Shamt,
  output [15:0] Inmediate,
  output [4:0] RD,
  output [4:0] RT,
  output [4:0] RS,
  output [5:0] OPCODE,
  output [25:0] JumAdd
);

  wire J, not_1_out, or_1_out, R;

  Comparator #(.width(6)) comparator_1 (.a(INPUTID[31:26]), .b(6'b000010), .eq(J));  // open: gt, lt
  Multiplexer #(.width(26)) multiplexer_1 (.in1(INPUTID[25:0]), .out(JumAdd), .sel(J));  // open: in0
  or or_1 (or_1_out, R, J);
  Multiplexer #(.width(16)) multiplexer_2 (.in1(INPUTID[15:0]), .out(Inmediate), .sel(not_1_out));  // open: in0
  not not_1 (not_1_out, or_1_out);
  Comparator #(.width(6)) comparator_2 (.a(INPUTID[31:26]), .b({6{1'b0}}), .eq(R));  // open: gt, lt
  Multiplexer #(.width(16)) multiplexer_3 (.in1(INPUTID[15:0]), .out({RD, Shamt, Funct}), .sel(R));  // open: in0

  assign OPCODE = INPUTID[31:26];
  assign RS = INPUTID[25:21];
  assign RT = INPUTID[20:16];

  // Other names for the same wires on the sheet: OP[5:0] = INPUTID[31:26]; JUMP[25:0] = JumAdd

  // Notes on the sheet:
  //   Cuando es J
  //   Cuando es R
endmodule

module UC (
  input  [5:0] opcode,
  output regdst,
  output regwrite,
  output jump,
  output bne,
  output beq,
  output alusrc,
  output memToReg,
  output memRead,
  output memWrite,
  output [1:0] ALU
);

  wire and_2_out, and_3_out, not_1_out, not_2_out, not_3_out, not_4_out;

  not not_1 (not_1_out, opcode[3]);
  not not_2 (not_2_out, opcode[2]);
  not not_3 (not_3_out, opcode[1]);
  not not_4 (not_4_out, opcode[0]);
  and and_1 (regdst, not_1_out, not_2_out, not_3_out);
  and and_2 (and_2_out, not_2_out, not_3_out);
  and and_3 (and_3_out, opcode[5], not_1_out);
  and and_4 (jump, opcode[1], not_4_out);
  and and_5 (bne, not_3_out, opcode[0]);
  and and_6 (beq, opcode[2], not_4_out);
  or or_1 (alusrc, opcode[3], opcode[5]);
  and and_7 (memToReg, opcode[5], not_1_out);
  and and_8 (memRead, opcode[5], not_1_out);
  and and_9 (memWrite, opcode[3], opcode[1]);
  and and_10 (ALU[1], not_1_out, not_2_out, not_3_out);
  or or_2 (regwrite, and_2_out, and_3_out);

  assign ALU[0] = opcode[2];
endmodule

module DebugComponent (
  input  [5:0] opCode,
  input  [5:0] funct,
  output Addi,
  output Load,
  output Store,
  output BEQ,
  output BNQ,
  output Jump,
  output None,
  output Add,
  output Sub,
  output AAnd,
  output OOr
);

  wire nonoOrR;

  debugStep1 debugstep1_1 (
    .opcode(opCode), .noneOrR(nonoOrR), .addi(Addi), .load(Load), .store(Store), .beq(BEQ), .bnq(BNQ),
    .jump(Jump));
  debugStep2 debugstep2_1 (.noneOrR(nonoOrR), .funct(funct), .none(None), .add(Add), .sub(Sub), .aand(AAnd), .oor(OOr));
endmodule

module debugStep1 (
  input  [5:0] opcode,
  output noneOrR,
  output addi,
  output load,
  output store,
  output beq,
  output bnq,
  output jump
);

  wire not_1_out, not_2_out, not_3_out, not_4_out, not_5_out, not_6_out;

  not not_1 (not_1_out, opcode[5]);
  not not_2 (not_2_out, opcode[4]);
  not not_3 (not_3_out, opcode[3]);
  not not_4 (not_4_out, opcode[2]);
  not not_5 (not_5_out, opcode[1]);
  not not_6 (not_6_out, opcode[0]);
  and and_1 (noneOrR, not_1_out, not_2_out, not_3_out, not_4_out, not_5_out, not_6_out);
  and and_2 (addi, not_1_out, not_2_out, opcode[3], not_4_out, not_5_out, not_6_out);
  and and_3 (load, opcode[5], not_2_out, not_3_out, not_4_out, opcode[1], opcode[0]);
  and and_4 (store, opcode[5], not_2_out, opcode[3], not_4_out, opcode[1], opcode[0]);
  and and_5 (beq, not_1_out, not_2_out, not_3_out, opcode[2], not_5_out, not_6_out);
  and and_6 (bnq, not_1_out, not_2_out, not_3_out, opcode[2], not_5_out, opcode[0]);
  and and_7 (jump, not_1_out, not_2_out, not_3_out, not_4_out, opcode[1], not_6_out);
endmodule

module debugStep2 (
  input  noneOrR,
  input  [5:0] funct,
  output none,
  output add,
  output sub,
  output aand,
  output oor
);

  wire not_1_out, not_2_out, not_3_out, not_4_out, not_5_out, not_6_out;

  not not_1 (not_1_out, funct[5]);
  not not_2 (not_2_out, funct[4]);
  not not_3 (not_3_out, funct[3]);
  not not_4 (not_4_out, funct[2]);
  not not_5 (not_5_out, funct[1]);
  not not_6 (not_6_out, funct[0]);
  and and_1 (none, noneOrR, not_1_out, not_2_out, not_3_out, not_4_out, not_5_out, not_6_out);
  and and_2 (add, noneOrR, funct[5], not_2_out, not_3_out, not_4_out, not_5_out, not_6_out);
  and and_3 (sub, noneOrR, funct[5], not_2_out, not_3_out, not_4_out, funct[1], not_6_out);
  and and_4 (aand, noneOrR, funct[5], not_2_out, not_3_out, funct[2], not_5_out, not_6_out);
  and and_5 (oor, noneOrR, funct[5], not_2_out, not_3_out, funct[2], not_5_out, funct[0]);
endmodule

module UCALU (
  input  [1:0] ALUOP,
  input  [5:0] FUNC,
  output [1:0] OUTPUT
);

  wire and_1_out, and_2_out, and_3_out, and_4_out, not_1_out, not_2_out, not_3_out, not_4_out, not_5_out,
       not_6_out, not_7_out;

  not not_1 (not_1_out, ALUOP[1]);
  not not_2 (not_2_out, ALUOP[0]);
  not not_3 (not_3_out, FUNC[4]);
  not not_4 (not_4_out, FUNC[3]);
  not not_5 (not_5_out, FUNC[2]);
  not not_6 (not_6_out, FUNC[1]);
  not not_7 (not_7_out, FUNC[0]);
  or or_1 (OUTPUT[1], not_1_out, and_1_out);
  and and_1 (and_1_out, not_2_out, FUNC[5], not_3_out, not_4_out, not_5_out, not_7_out);
  and and_2 (and_2_out, ALUOP[1], not_2_out, FUNC[5], not_3_out, not_4_out, not_5_out, FUNC[1], not_7_out);
  and and_3 (and_3_out, ALUOP[1], not_2_out, FUNC[5], not_3_out, not_4_out, FUNC[2], not_6_out, FUNC[0]);
  or or_2 (OUTPUT[0], and_2_out, and_3_out, and_4_out);
  and and_4 (and_4_out, not_1_out, ALUOP[0]);
endmodule

module UR (
  input  [31:0] BUSW,
  input  RESET,
  input  [4:0] RS,
  input  CLK,
  input  [4:0] RT,
  input  [4:0] RW,
  input  REGWRITE,
  output [31:0] RegA,
  output [31:0] RegB
);

  wire EnaT0, EnaT1, EnaT2, EnaT3, EnaT4, EnaT5, EnaT6, EnaT7, EnaT8, EnaT9, EnaT10, EnaT11, EnaT12, EnaT13,
       EnaT14, EnaT15, EnaT16, EnaT17, EnaT18, EnaT19, EnaT20, EnaT21, EnaT22, EnaT23;
  wire [31:0] R8, R9, R10, R11, R12, R13, R14, R15, R16, R17, R18, R19, R20, R21, R22, R23, R24, R25, R26,
       R27, R28, R29, R30, R31;

  Demultiplexer #(.select(5)) demultiplexer_1 (
    .out8(EnaT0), .out9(EnaT1), .out10(EnaT2), .out11(EnaT3), .out12(EnaT4), .out13(EnaT5), .out14(EnaT6),
    .out15(EnaT7), .out16(EnaT8), .out17(EnaT9), .out18(EnaT10), .out19(EnaT11), .out20(EnaT12),
    .out21(EnaT13), .out22(EnaT14), .out23(EnaT15), .out24(EnaT16), .out25(EnaT17), .out26(EnaT18),
    .out27(EnaT19), .out28(EnaT20), .out29(EnaT21), .out30(EnaT22), .out31(EnaT23), .in(REGWRITE), .sel(RW));  // open: out0, out1, out2, out3, out4, out5, out6, out7
  Register #(.trigger("falling"), .width(32)) t0 (.D(BUSW), .en(EnaT0), .Q(R8), .clk(CLK), .clr(RESET));
  Register #(.trigger("falling"), .width(32)) t1 (.D(BUSW), .en(EnaT1), .Q(R9), .clk(CLK), .clr(RESET));
  Register #(.trigger("falling"), .width(32)) t2 (.D(BUSW), .en(EnaT2), .Q(R10), .clk(CLK), .clr(RESET));
  Register #(.trigger("falling"), .width(32)) t3 (.D(BUSW), .en(EnaT3), .Q(R11), .clk(CLK), .clr(RESET));
  Register #(.trigger("falling"), .width(32)) t4 (.D(BUSW), .en(EnaT4), .Q(R12), .clk(CLK), .clr(RESET));
  Register #(.trigger("falling"), .width(32)) t5 (.D(BUSW), .en(EnaT5), .Q(R13), .clk(CLK), .clr(RESET));
  Register #(.trigger("falling"), .width(32)) t6 (.D(BUSW), .en(EnaT6), .Q(R14), .clk(CLK), .clr(RESET));
  Register #(.trigger("falling"), .width(32)) t7 (.D(BUSW), .en(EnaT7), .Q(R15), .clk(CLK), .clr(RESET));
  Register #(.trigger("falling"), .width(32)) s0 (.D(BUSW), .en(EnaT8), .Q(R16), .clk(CLK), .clr(RESET));
  Register #(.trigger("falling"), .width(32)) s1 (.D(BUSW), .en(EnaT9), .Q(R17), .clk(CLK), .clr(RESET));
  Register #(.trigger("falling"), .width(32)) s2 (.D(BUSW), .en(EnaT10), .Q(R18), .clk(CLK), .clr(RESET));
  Register #(.trigger("falling"), .width(32)) s3 (.D(BUSW), .en(EnaT11), .Q(R19), .clk(CLK), .clr(RESET));
  Register #(.trigger("falling"), .width(32)) s4 (.D(BUSW), .en(EnaT12), .Q(R20), .clk(CLK), .clr(RESET));
  Register #(.trigger("falling"), .width(32)) s5 (.D(BUSW), .en(EnaT13), .Q(R21), .clk(CLK), .clr(RESET));
  Register #(.trigger("falling"), .width(32)) s6 (.D(BUSW), .en(EnaT14), .Q(R22), .clk(CLK), .clr(RESET));
  Register #(.trigger("falling"), .width(32)) s7 (.D(BUSW), .en(EnaT15), .Q(R23), .clk(CLK), .clr(RESET));
  Register #(.trigger("falling"), .width(32)) t8 (.D(BUSW), .en(EnaT16), .Q(R24), .clk(CLK), .clr(RESET));
  Register #(.trigger("falling"), .width(32)) t17 (.D(BUSW), .en(EnaT17), .Q(R25), .clk(CLK), .clr(RESET));
  Register #(.trigger("falling"), .width(32)) t18 (.D(BUSW), .en(EnaT18), .Q(R26), .clk(CLK), .clr(RESET));
  Register #(.trigger("falling"), .width(32)) t19 (.D(BUSW), .en(EnaT19), .Q(R27), .clk(CLK), .clr(RESET));
  Register #(.trigger("falling"), .width(32)) t20 (.D(BUSW), .en(EnaT20), .Q(R28), .clk(CLK), .clr(RESET));
  Register #(.trigger("falling"), .width(32)) t21 (.D(BUSW), .en(EnaT21), .Q(R29), .clk(CLK), .clr(RESET));
  Register #(.trigger("falling"), .width(32)) t22 (.D(BUSW), .en(EnaT22), .Q(R30), .clk(CLK), .clr(RESET));
  Register #(.trigger("falling"), .width(32)) t23 (.D(BUSW), .en(EnaT23), .Q(R31), .clk(CLK), .clr(RESET));
  Multiplexer #(.select(5), .width(32)) multiplexer_1 (
    .in8(R8), .in9(R9), .in10(R10), .in11(R11), .in12(R12), .in13(R13), .in14(R14), .in15(R15), .in16(R16),
    .in17(R17), .in18(R18), .in19(R19), .in20(R20), .in21(R21), .in22(R22), .in23(R23), .in24(R24),
    .in25(R25), .in26(R26), .in27(R27), .in28(R28), .in29(R29), .in30(R30), .in31(R31), .out(RegA), .sel(RS));  // open: in0, in1, in2, in3, in4, in5, in6, in7
  Multiplexer #(.select(5), .width(32)) multiplexer_2 (
    .in8(R8), .in9(R9), .in10(R10), .in11(R11), .in12(R12), .in13(R13), .in14(R14), .in15(R15), .in16(R16),
    .in17(R17), .in18(R18), .in19(R19), .in20(R20), .in21(R21), .in22(R22), .in23(R23), .in24(R24),
    .in25(R25), .in26(R26), .in27(R27), .in28(R28), .in29(R29), .in30(R30), .in31(R31), .out(RegB), .sel(RT));  // open: in0, in1, in2, in3, in4, in5, in6, in7

  // Other names for the same wires on the sheet: DT0[31:0] = BUSW; DT1[31:0] = BUSW; DT2[31:0] = BUSW;
  //   DT3[31:0] = BUSW; DT4[31:0] = BUSW; DT5[31:0] = BUSW; DT6[31:0] = BUSW; DT7[31:0] = BUSW; DT8[31:0] = BUSW;
  //   DT9[31:0] = BUSW; DT10[31:0] = BUSW; DT11[31:0] = BUSW; DT12[31:0] = BUSW; DT13[31:0] = BUSW; DT14[31:0] = BUSW;
  //   DT15[31:0] = BUSW; DT16[31:0] = BUSW; DT17[31:0] = BUSW; DT18[31:0] = BUSW; DT19[31:0] = BUSW;
  //   DT20[31:0] = BUSW; DT21[31:0] = BUSW; DT22[31:0] = BUSW; DT23[31:0] = BUSW; TSELECTORA[4:0] = RS;
  //   TSELECTORB[4:0] = RT; TSELECTORR[4:0] = RW
endmodule

module TSelector (
  input  [4:0] DIR,
  output [2:0] OUTPUT
);


  assign OUTPUT = DIR[2:0];
endmodule

module ALU (
  input  [1:0] ALUCTR,
  input  [31:0] BUSA,
  input  [31:0] BUSB,
  output [31:0] Data,
  output ZERO
);

  wire [31:0] ADDF, ANDF, ORF, SUBF;

  assign ANDF = BUSA & BUSB;  // AND_Gate and_1, 32 bits wide
  assign ORF = BUSA | BUSB;  // OR_Gate or_1, 32 bits wide
  Adder #(.width(32)) adder_1 (.a(BUSA), .b(BUSB), .out(ADDF));  // open: cin, cout
  Subtractor #(.width(32)) subtractor_1 (.a(BUSA), .b(BUSB), .out(SUBF));  // open: bin, bout
  // Probe on ADDF
  // Probe on SUBF
  // Probe on ANDF
  // Probe on ANDF
  // Probe on nothing
  Multiplexer #(.select(2), .width(32)) multiplexer_1 (
    .in0(ANDF), .in1(ORF), .in2(ADDF), .in3(SUBF), .out(Data), .sel(ALUCTR));
  Comparator #(.width(32)) comparator_1 (.a(Data), .b({32{1'b0}}), .eq(ZERO));  // open: gt, lt

  // Other names for the same wires on the sheet: A[31:0] = BUSA; ALUCTRL[1:0] = ALUCTR; B[31:0] = BUSB

  // Notes on the sheet:
  //   AND(00)
  //   OR(01)
  //   ADD(10)
  //   SUB(11)
endmodule

module Branch (
  input  [23:0] pcMasUno,
  input  [15:0] IMM,
  input  ZERO,
  input  beq,
  input  benq,
  output [23:0] outValue
);

  wire and_1_out, and_2_out, not_1_out, or_1_out;
  wire [23:0] adder_1_out, bit_extender_1_out, multiplexer_1_out, subtractor_1_out;

  assign bit_extender_1_out = {{9{IMM[14]}}, IMM[14:0]};  // Bit_Extender bit_extender_1
  Adder #(.width(24)) adder_1 (.a(pcMasUno), .b(bit_extender_1_out), .out(adder_1_out));  // open: cin, cout
  Subtractor #(.width(24)) subtractor_1 (
    .a(pcMasUno), .b(bit_extender_1_out), .out(subtractor_1_out));  // open: bin, bout
  Multiplexer #(.width(24)) multiplexer_1 (
    .in0(adder_1_out), .in1(subtractor_1_out), .out(multiplexer_1_out), .sel(IMM[15]));
  or or_1 (or_1_out, and_1_out, and_2_out);
  and and_1 (and_1_out, ZERO, beq);
  not not_1 (not_1_out, ZERO);
  Multiplexer #(.width(24)) multiplexer_2 (.in0(pcMasUno), .in1(multiplexer_1_out), .out(outValue), .sel(or_1_out));
  and and_2 (and_2_out, not_1_out, benq);
endmodule

module Ifetch (
  input  [23:0] PCmasUno,
  input  [31:0] Instruction,
  input  CLK,
  input  RESET,
  input  [4:0] RWMesa2,
  input  [4:0] RWMesa3,
  input  NoneIDEX,
  input  NoneEXMem,
  output [23:0] PCmasUnoResult,
  output [31:0] InstructionResult,
  output HAZARD,
  output [5:0] FUNCTIF,
  output [5:0] OPCODEIF
);

  wire and_1_out, comparator_1_eq, hazarddetection_1_out_7, not_1_out, not_2_out, not_3_out;
  wire [4:0] id_1_rs, id_1_rt;
  wire [31:0] InstructionResult_t;

  not not_1 (not_1_out, 1'b0);
  not not_2 (not_2_out, 1'b0);
  Register #(.width(24)) register_1 (.D(PCmasUno), .en(not_2_out), .Q(PCmasUnoResult), .clk(CLK), .clr(RESET));
  Register #(.width(32)) register_2 (.D(Instruction), .en(not_1_out), .Q(InstructionResult_t), .clk(CLK), .clr(RESET));
  ID id_1 (
    .INPUTID(InstructionResult_t), .RT(id_1_rt), .RS(id_1_rs));  // open: Funct, Shamt, Inmediate, RD, OPCODE, JumAdd
  Multiplexer #(.width(32)) multiplexer_1 (
    .in0(InstructionResult_t), .in1({32{1'b0}}), .out(InstructionResult), .sel(1'b0));
  HAZARDDETECTION hazarddetection_1 (
    .RS(id_1_rs), .RT(id_1_rt), .RWMesa2(RWMesa2), .RWMesa3(RWMesa3), .NoneIDEX(NoneIDEX),
    .NoneEXMem(NoneEXMem), .out_7(hazarddetection_1_out_7));
  ID id_2 (
    .INPUTID(InstructionResult_t), .Funct(FUNCTIF), .OPCODE(OPCODEIF));  // open: Shamt, Inmediate, RD, RT, RS, JumAdd
  Comparator #(.width(24)) comparator_1 (.a({24{1'b0}}), .b(PCmasUnoResult), .eq(comparator_1_eq));  // open: gt, lt
  not not_3 (not_3_out, comparator_1_eq);
  // Probe on InstructionResult_t
  and and_1 (and_1_out, hazarddetection_1_out_7, not_3_out);

  assign HAZARD = 1'b0;

  // Other names for the same wires on the sheet: InstructionTest[31:0] = InstructionResult_t
endmodule

module ID_EX_Reg (
  input  [23:0] PCmasUnoIfetch,
  input  [15:0] IMM,
  input  [31:0] Ra,
  input  [31:0] Rb,
  input  [4:0] RT,
  input  [4:0] RD,
  input  [5:0] OPCODE,
  input  [5:0] Funct,
  input  RESET,
  input  CLK,
  input  [1:0] ALUOP,
  input  REGDST,
  input  ALUSRC,
  input  MEMREG,
  input  MEMWR,
  input  REGWRITE,
  input  [4:0] RS,
  output [23:0] PCmasUnoEX,
  output [15:0] IMMEX,
  output [31:0] BusA,
  output [31:0] BusB,
  output [4:0] RTEX,
  output [4:0] RDEX,
  output [5:0] OPCODEEX,
  output [5:0] FunctEX,
  output [1:0] ALUOPEX,
  output REGDSTEX,
  output ALUSRCEX,
  output MEMREGEX,
  output MEMWREX,
  output REGWRITEX,
  output [4:0] RSEX
);

  wire debugcomponent_1_aand, debugcomponent_1_add, debugcomponent_1_addi, debugcomponent_1_beq,
       debugcomponent_1_bnq, debugcomponent_1_jump, debugcomponent_1_load, debugcomponent_1_none,
       debugcomponent_1_oor, debugcomponent_1_store, debugcomponent_1_sub;

  Register #(.width(1)) register_1 (.D(ALUSRC), .Q(ALUSRCEX), .clk(CLK), .clr(RESET));  // open: en
  Register #(.width(24)) register_2 (.D(PCmasUnoIfetch), .Q(PCmasUnoEX), .clk(CLK), .clr(RESET));  // open: en
  Register #(.width(32)) register_3 (.D(Ra), .Q(BusA), .clk(CLK), .clr(RESET));  // open: en
  Register #(.width(5)) register_4 (.D(RT), .Q(RTEX), .clk(CLK), .clr(RESET));  // open: en
  Register #(.width(6)) register_5 (.D(OPCODE), .Q(OPCODEEX), .clk(CLK), .clr(RESET));  // open: en
  Register #(.width(2)) register_6 (.D(ALUOP), .Q(ALUOPEX), .clk(CLK), .clr(RESET));  // open: en
  Register #(.width(1)) register_7 (.D(REGWRITE), .Q(REGWRITEX), .clk(CLK), .clr(RESET));  // open: en
  Register #(.width(5)) register_8 (.D(RS), .Q(RSEX), .clk(CLK), .clr(RESET));  // open: en
  Register #(.width(16)) register_9 (.D(IMM), .Q(IMMEX), .clk(CLK), .clr(RESET));  // open: en
  Register #(.width(32)) register_10 (.D(Rb), .Q(BusB), .clk(CLK), .clr(RESET));  // open: en
  Register #(.width(5)) register_11 (.D(RD), .Q(RDEX), .clk(CLK), .clr(RESET));  // open: en
  Register #(.width(6)) register_12 (.D(Funct), .Q(FunctEX), .clk(CLK), .clr(RESET));  // open: en
  Register #(.width(1)) register_13 (.D(REGDST), .Q(REGDSTEX), .clk(CLK), .clr(RESET));  // open: en
  Register #(.width(1)) register_14 (.D(MEMREG), .Q(MEMREGEX), .clk(CLK), .clr(RESET));  // open: en
  LED led_1 (.in(debugcomponent_1_addi));
  DebugComponent debugcomponent_1 (
    .opCode(OPCODEEX), .funct(FunctEX), .Addi(debugcomponent_1_addi), .Load(debugcomponent_1_load),
    .Store(debugcomponent_1_store), .BEQ(debugcomponent_1_beq), .BNQ(debugcomponent_1_bnq),
    .Jump(debugcomponent_1_jump), .None(debugcomponent_1_none), .Add(debugcomponent_1_add),
    .Sub(debugcomponent_1_sub), .AAnd(debugcomponent_1_aand), .OOr(debugcomponent_1_oor));
  LED led_2 (.in(debugcomponent_1_load));
  LED led_3 (.in(debugcomponent_1_store));
  LED led_4 (.in(debugcomponent_1_beq));
  LED led_5 (.in(debugcomponent_1_bnq));
  LED led_6 (.in(debugcomponent_1_jump));
  LED led_7 (.in(debugcomponent_1_none));
  LED led_8 (.in(debugcomponent_1_add));
  LED led_9 (.in(debugcomponent_1_sub));
  LED led_10 (.in(debugcomponent_1_aand));
  LED led_11 (.in(debugcomponent_1_oor));
  Register #(.width(1)) register_15 (.D(MEMWR), .Q(MEMWREX), .clk(CLK), .clr(RESET));  // open: en

  // Other names for the same wires on the sheet: RaEX[31:0] = BusA; RbEX[31:0] = BusB; REGWRITEEX = REGWRITEX
endmodule

module EX_Mem_Reg (
  input  [23:0] PCmasUnoEX,
  input  [31:0] ALUData,
  input  [31:0] BusB,
  input  Zero,
  input  [4:0] RW,
  input  [5:0] OPCODE,
  input  [5:0] FunctEX,
  input  CLK,
  input  RESET,
  input  MEMWR,
  input  MEMREG,
  input  REGWRITE,
  output [23:0] PCmasUnoMem,
  output [5:0] OPCODEMem,
  output [31:0] ALUDataMem,
  output [31:0] BusBMem,
  output ZeroMem,
  output [4:0] RWMem,
  output [5:0] FunctMem,
  output MEMWREX,
  output MEMREGMEM,
  output REGWRITEMEM
);

  wire debugcomponent_1_aand, debugcomponent_1_add, debugcomponent_1_addi, debugcomponent_1_beq,
       debugcomponent_1_bnq, debugcomponent_1_jump, debugcomponent_1_load, debugcomponent_1_none,
       debugcomponent_1_oor, debugcomponent_1_store, debugcomponent_1_sub;

  Register #(.width(24)) register_1 (.D(PCmasUnoEX), .Q(PCmasUnoMem), .clk(CLK), .clr(RESET));  // open: en
  Register #(.width(32)) register_2 (.D(ALUData), .Q(ALUDataMem), .clk(CLK), .clr(RESET));  // open: en
  Register #(.width(1)) register_3 (.D(Zero), .Q(ZeroMem), .clk(CLK), .clr(RESET));  // open: en
  Register #(.width(1)) register_4 (.D(MEMWR), .Q(MEMWREX), .clk(CLK), .clr(RESET));  // open: en
  Register #(.width(1)) register_5 (.D(REGWRITE), .Q(REGWRITEMEM), .clk(CLK), .clr(RESET));  // open: en
  Register #(.width(6)) register_6 (.D(FunctEX), .Q(FunctMem), .clk(CLK), .clr(RESET));  // open: en
  Register #(.width(1)) register_7 (.D(MEMREG), .Q(MEMREGMEM), .clk(CLK), .clr(RESET));  // open: en
  Register #(.width(6)) register_8 (.D(OPCODE), .Q(OPCODEMem), .clk(CLK), .clr(RESET));  // open: en
  Register #(.width(32)) register_9 (.D(BusB), .Q(BusBMem), .clk(CLK), .clr(RESET));  // open: en
  Register #(.width(5)) register_10 (.D(RW), .Q(RWMem), .clk(CLK), .clr(RESET));  // open: en
  LED led_1 (.in(debugcomponent_1_addi));
  DebugComponent debugcomponent_1 (
    .opCode(OPCODEMem), .funct(FunctMem), .Addi(debugcomponent_1_addi), .Load(debugcomponent_1_load),
    .Store(debugcomponent_1_store), .BEQ(debugcomponent_1_beq), .BNQ(debugcomponent_1_bnq),
    .Jump(debugcomponent_1_jump), .None(debugcomponent_1_none), .Add(debugcomponent_1_add),
    .Sub(debugcomponent_1_sub), .AAnd(debugcomponent_1_aand), .OOr(debugcomponent_1_oor));
  LED led_2 (.in(debugcomponent_1_load));
  LED led_3 (.in(debugcomponent_1_store));
  LED led_4 (.in(debugcomponent_1_beq));
  LED led_5 (.in(debugcomponent_1_bnq));
  LED led_6 (.in(debugcomponent_1_jump));
  LED led_7 (.in(debugcomponent_1_none));
  LED led_8 (.in(debugcomponent_1_add));
  LED led_9 (.in(debugcomponent_1_sub));
  LED led_10 (.in(debugcomponent_1_aand));
  LED led_11 (.in(debugcomponent_1_oor));

  // Other names for the same wires on the sheet: BusBEX[31:0] = BusB; Funct[5:0] = FunctEX; MEMWMEM = MEMWREX
endmodule

module Mem_Wr_Reg (
  input  [31:0] ALUDataMem,
  input  [31:0] DataMemory,
  input  [4:0] RWMem,
  input  [5:0] OPCODEMem,
  input  [5:0] FunctMem,
  input  CLK,
  input  RESET,
  input  MEMREG,
  input  REGWR,
  output [31:0] ALUDataWr,
  output [31:0] DataMemoryWr,
  output [4:0] RWWr,
  output [5:0] OPCODEWr,
  output [5:0] FunctWr,
  output MEMREGWRWR,
  output REGWRWR
);

  wire debugcomponent_1_aand, debugcomponent_1_add, debugcomponent_1_addi, debugcomponent_1_beq,
       debugcomponent_1_bnq, debugcomponent_1_jump, debugcomponent_1_load, debugcomponent_1_none,
       debugcomponent_1_oor, debugcomponent_1_store, debugcomponent_1_sub;

  Register #(.width(1)) register_1 (.D(MEMREG), .Q(MEMREGWRWR), .clk(CLK), .clr(RESET));  // open: en
  Register #(.width(32)) register_2 (.D(ALUDataMem), .Q(ALUDataWr), .clk(CLK), .clr(RESET));  // open: en
  Register #(.width(5)) register_3 (.D(RWMem), .Q(RWWr), .clk(CLK), .clr(RESET));  // open: en
  Register #(.width(6)) register_4 (.D(FunctMem), .Q(FunctWr), .clk(CLK), .clr(RESET));  // open: en
  Register #(.width(1)) register_5 (.D(REGWR), .Q(REGWRWR), .clk(CLK), .clr(RESET));  // open: en
  LED led_1 (.in(debugcomponent_1_addi));
  DebugComponent debugcomponent_1 (
    .opCode(OPCODEWr), .funct(FunctWr), .Addi(debugcomponent_1_addi), .Load(debugcomponent_1_load),
    .Store(debugcomponent_1_store), .BEQ(debugcomponent_1_beq), .BNQ(debugcomponent_1_bnq),
    .Jump(debugcomponent_1_jump), .None(debugcomponent_1_none), .Add(debugcomponent_1_add),
    .Sub(debugcomponent_1_sub), .AAnd(debugcomponent_1_aand), .OOr(debugcomponent_1_oor));
  LED led_2 (.in(debugcomponent_1_load));
  LED led_3 (.in(debugcomponent_1_store));
  LED led_4 (.in(debugcomponent_1_beq));
  LED led_5 (.in(debugcomponent_1_bnq));
  LED led_6 (.in(debugcomponent_1_jump));
  LED led_7 (.in(debugcomponent_1_none));
  LED led_8 (.in(debugcomponent_1_add));
  LED led_9 (.in(debugcomponent_1_sub));
  LED led_10 (.in(debugcomponent_1_aand));
  LED led_11 (.in(debugcomponent_1_oor));
  Register #(.width(32)) register_6 (.D(DataMemory), .Q(DataMemoryWr), .clk(CLK), .clr(RESET));  // open: en
  Register #(.width(6)) register_7 (.D(OPCODEMem), .Q(OPCODEWr), .clk(CLK), .clr(RESET));  // open: en

  // Other names for the same wires on the sheet: ALUData[31:0] = ALUDataMem; Funct[5:0] = FunctMem;
  //   MEMREGWR = MEMREGWRWR
endmodule

module HAZARDDETECTION (
  input  [4:0] RS,
  input  [4:0] RT,
  input  [4:0] RWMesa2,
  input  [4:0] RWMesa3,
  input  NoneIDEX,
  input  NoneEXMem,
  output out_7
);

  wire and_1_out, and_2_out, comparator_1_eq, comparator_2_eq, comparator_3_eq, comparator_4_eq, not_1_out,
       not_2_out, or_1_out, or_2_out;

  Comparator #(.width(5)) comparator_1 (.a(RS), .b(RWMesa2), .eq(comparator_1_eq));  // open: gt, lt
  Comparator #(.width(5)) comparator_2 (.a(RT), .b(RWMesa2), .eq(comparator_2_eq));  // open: gt, lt
  Comparator #(.width(5)) comparator_3 (.a(RT), .b(RWMesa3), .eq(comparator_3_eq));  // open: gt, lt
  Comparator #(.width(5)) comparator_4 (.a(RS), .b(RWMesa3), .eq(comparator_4_eq));  // open: gt, lt
  or or_1 (or_1_out, comparator_1_eq, comparator_2_eq);
  or or_2 (or_2_out, comparator_3_eq, comparator_4_eq);
  not not_1 (not_1_out, NoneIDEX);
  not not_2 (not_2_out, NoneEXMem);
  and and_1 (and_1_out, or_1_out, not_1_out);
  and and_2 (and_2_out, or_2_out, not_2_out);
  or or_3 (out_7, and_1_out, and_2_out);
endmodule

module ForwardingUnit (
  input  [4:0] RS,
  input  [4:0] RT,
  input  [4:0] RWMesa3,
  input  [4:0] RWMesa4,
  input  NoneEXMEM,
  input  NoneMEMWR,
  output [1:0] ForwardA,
  output [1:0] ForwardB
);

  wire and_1_out, and_2_out, comparator_1_eq, comparator_2_eq, comparator_3_eq, comparator_4_eq,
       comparator_5_eq, comparator_6_eq, comparator_7_eq, comparator_8_eq, IsHazard, not_1_out, not_2_out,
       or_1_out, or_2_out;
  wire [1:0] multiplexer_1_out, multiplexer_2_out, multiplexer_3_out, multiplexer_4_out;

  Comparator #(.width(5)) comparator_1 (.a(RS), .b(RWMesa3), .eq(comparator_1_eq));  // open: gt, lt
  Comparator #(.width(5)) comparator_2 (.a(RT), .b(RWMesa3), .eq(comparator_2_eq));  // open: gt, lt
  Comparator #(.width(5)) comparator_3 (.a(RT), .b(RWMesa4), .eq(comparator_3_eq));  // open: gt, lt
  Comparator #(.width(5)) comparator_4 (.a(RS), .b(RWMesa4), .eq(comparator_4_eq));  // open: gt, lt
  Comparator #(.width(5)) comparator_5 (.a(RS), .b(RWMesa3), .eq(comparator_5_eq));  // open: gt, lt
  Comparator #(.width(5)) comparator_6 (.a(RWMesa4), .b(RS), .eq(comparator_6_eq));  // open: gt, lt
  Comparator #(.width(5)) comparator_7 (.a(RT), .b(RWMesa3), .eq(comparator_7_eq));  // open: gt, lt
  Comparator #(.width(5)) comparator_8 (.a(RWMesa4), .b(RT), .eq(comparator_8_eq));  // open: gt, lt
  Multiplexer #(.width(2)) multiplexer_1 (.in0(2'b00), .in1(2'b01), .out(multiplexer_1_out), .sel(comparator_6_eq));
  Multiplexer #(.width(2)) multiplexer_2 (.in0(2'b00), .in1(2'b01), .out(multiplexer_2_out), .sel(comparator_8_eq));
  or or_1 (or_1_out, comparator_1_eq, comparator_2_eq);
  or or_2 (or_2_out, comparator_3_eq, comparator_4_eq);
  Multiplexer #(.width(2)) multiplexer_3 (
    .in0(multiplexer_1_out), .in1(2'b10), .out(multiplexer_3_out), .sel(comparator_5_eq));
  Multiplexer #(.width(2)) multiplexer_4 (
    .in0(multiplexer_2_out), .in1(2'b10), .out(multiplexer_4_out), .sel(comparator_7_eq));
  not not_1 (not_1_out, NoneEXMEM);
  not not_2 (not_2_out, NoneMEMWR);
  and and_1 (and_1_out, or_1_out, not_1_out);
  and and_2 (and_2_out, or_2_out, not_2_out);
  Multiplexer #(.width(2)) multiplexer_5 (.in0(2'b00), .in1(multiplexer_3_out), .out(ForwardA), .sel(IsHazard));
  Multiplexer #(.width(2)) multiplexer_6 (.in0(2'b00), .in1(multiplexer_4_out), .out(ForwardB), .sel(IsHazard));
  or or_3 (IsHazard, and_1_out, and_2_out);
endmodule
