// Logisim project CPU1-RCAGAMEZ.circ as structural Verilog: 11 circuits, main circuit main
module main (
);

  wire ALUSRC, beq, bne, CLK, debugcomponent_1_aand, debugcomponent_1_add, debugcomponent_1_addi,
       debugcomponent_1_beq, debugcomponent_1_bnq, debugcomponent_1_jump, debugcomponent_1_load,
       debugcomponent_1_none, debugcomponent_1_oor, debugcomponent_1_store, debugcomponent_1_sub,
       JumpCondition, MemW, MTR, not_1_out, REGDST, REGWRITE, Rst, uc_1_memread, ZERO;
  wire [1:0] ALUCTRL, uc_1_alu;
  wire [4:0] id_1_shamt, multiplexer_1_out, RD, RS, RT;
  wire [5:0] FUNC, OPCODE;
  wire [15:0] IMM;
  wire [23:0] bit_extender_2_out, bit_extender_3_out, branch_1_outvalue, Iter, PC, PcMasUno;
  wire [25:0] JumpAdd;
  wire [31:0] alu_1_data, bit_extender_1_out, BusB, multiplexer_2_out, multiplexer_4_out, ram_1_dout,
       ram_2_dout, ur_1_ra;

  RAM #(.addrWidth(24), .dataWidth(32), .enables("line")) ram_1 (.addr(Iter), .dout(ram_1_dout));  // open: we, clk, din
  Button button_1 (.out(Rst));
  Clock clock_1 (.out(CLK));
  Register #(.width(24)) register_1 (.D(PC), .Q(Iter), .clk(CLK), .clr(Rst));  // open: en
  Adder #(.width(24)) adder_1 (.a(Iter), .b(24'h1), .out(PcMasUno));  // open: cin, cout
  Multiplexer #(.width(5)) multiplexer_1 (.in0(RT), .in1(RD), .out(multiplexer_1_out), .sel(REGDST));
  LED led_1 (.in(debugcomponent_1_addi));
  DebugComponent debugcomponent_1 (
    .opCode(OPCODE), .funct(FUNC), .Addi(debugcomponent_1_addi), .Load(debugcomponent_1_load),
    .Store(debugcomponent_1_store), .BEQ(debugcomponent_1_beq), .BNQ(debugcomponent_1_bnq),
    .Jump(debugcomponent_1_jump), .None(debugcomponent_1_none), .Add(debugcomponent_1_add),
    .Sub(debugcomponent_1_sub), .AAnd(debugcomponent_1_aand), .OOr(debugcomponent_1_oor));
  LED led_2 (.in(debugcomponent_1_load));
  LED led_3 (.in(debugcomponent_1_store));
  LED led_4 (.in(debugcomponent_1_beq));
  LED led_5 (.in(debugcomponent_1_bnq));
  LED led_6 (.in(debugcomponent_1_jump));
  LED led_7 (.in(debugcomponent_1_none));
  LED led_8 (.in(debugcomponent_1_add));
  LED led_9 (.in(debugcomponent_1_sub));
  LED led_10 (.in(debugcomponent_1_aand));
  LED led_11 (.in(debugcomponent_1_oor));
  ID id_1 (
    .INPUTID(ram_1_dout), .Funct(FUNC), .Shamt(id_1_shamt), .Inmediate(IMM), .RD(RD), .RT(RT), .RS(RS),
    .OPCODE(OPCODE), .JumAdd(JumpAdd));
  // Probe on FUNC
  // Probe on id_1_shamt
  UR ur_1 (
    .BUSW(multiplexer_4_out), .RESET(Rst), .RS(RS), .CLK(CLK), .RT(RT), .RW(multiplexer_1_out),
    .REGWRITE(REGWRITE), .RA(ur_1_ra), .RB(BusB));
  assign bit_extender_1_out = {{16{IMM[15]}}, IMM};  // Bit_Extender bit_extender_1
  UC uc_1 (
    .opcode(OPCODE), .regdst(REGDST), .regwrite(REGWRITE), .jump(JumpCondition), .bne(bne), .beq(beq),
    .alusrc(ALUSRC), .memToReg(MTR), .memRead(uc_1_memread), .memWrite(MemW), .ALU(uc_1_alu));
  // Probe on uc_1_memread
  // Probe on uc_1_alu
  Multiplexer #(.width(32)) multiplexer_2 (.in0(BusB), .in1(bit_extender_1_out), .out(multiplexer_2_out), .sel(ALUSRC));
  Bit_Extender #(.in_width(26), .out_width(24)) bit_extender_2 (.in(JumpAdd), .out(bit_extender_2_out));
  Branch branch_1 (.pcMasUno(PcMasUno), .IMM(IMM), .ZERO(ZERO), .beq(beq), .benq(bne), .outValue(branch_1_outvalue));
  ALU alu_1 (.ALUCTR(ALUCTRL), .BUSA(ur_1_ra), .BUSB(multiplexer_2_out), .Data(alu_1_data), .ZERO(ZERO));
  Multiplexer #(.width(24)) multiplexer_3 (
    .in0(bit_extender_2_out), .in1(branch_1_outvalue), .out(PC), .sel(not_1_out));
  not not_1 (not_1_out, JumpCondition);
  Bit_Extender #(.in_width(32), .out_width(24)) bit_extender_3 (.in(alu_1_data), .out(bit_extender_3_out));
  UCALU ucalu_1 (.ALUOP(uc_1_alu), .FUNC(FUNC), .OUTPUT(ALUCTRL));
  RAM #(.addrWidth(24), .clearpin("true"), .dataWidth(32), .enables("line")) ram_2 (
    .addr(bit_extender_3_out), .we(MemW), .clk(CLK), .din(BusB), .dout(ram_2_dout), .clr(Rst));
  Multiplexer #(.width(32)) multiplexer_4 (.in0(alu_1_data), .in1(ram_2_dout), .out(multiplexer_4_out), .sel(MTR));

  // Notes on the sheet:
  //   ALU
endmodule

module ID (
  input  [31:0] INPUTID,
  output [5:0] Funct,
  output [4:0] Shamt,
  output [15:0] Inmediate,
  output [4:0] RD,
  output [4:0] RT,
  output [4:0] RS,
  output [5:0] OPCODE,
  output [25:0] JumAdd
);

  wire J, not_1_out, or_1_out, R;

  Comparator #(.width(6)) comparator_1 (.a(INPUTID[31:26]), .b(6'b000010), .eq(J));  // open: gt, lt
  Multiplexer #(.width(26)) multiplexer_1 (.in1(INPUTID[25:0]), .out(JumAdd), .sel(J));  // open: in0
  or or_1 (or_1_out, R, J);
  Multiplexer #(.width(16)) multiplexer_2 (.in1(INPUTID[15:0]), .out(Inmediate), .sel(not_1_out));  // open: in0
  not not_1 (not_1_out, or_1_out);
  Comparator #(.width(6)) comparator_2 (.a(INPUTID[31:26]), .b({6{1'b0}}), .eq(R));  // open: gt, lt
  Multiplexer #(.width(16)) multiplexer_3 (.in1(INPUTID[15:0]), .out({RD, Shamt, Funct}), .sel(R));  // open: in0

  assign OPCODE = INPUTID[31:26];
  assign RS = INPUTID[25:21];
  assign RT = INPUTID[20:16];

  // Other names for the same wires on the sheet: OP[5:0] = INPUTID[31:26]; JUMP[25:0] = JumAdd

  // Notes on the sheet:
  //   Cuando es J
  //   Cuando es R
endmodule

module UC (
  input  [5:0] opcode,
  output regdst,
  output regwrite,
  output jump,
  output bne,
  output beq,
  output alusrc,
  output memToReg,
  output memRead,
  output memWrite,
  output [1:0] ALU
);

  wire and_2_out, and_3_out, not_1_out, not_2_out, not_3_out, not_4_out;

  not not_1 (not_1_out, opcode[3]);
  not not_2 (not_2_out, opcode[2]);
  not not_3 (not_3_out, opcode[1]);
  not not_4 (not_4_out, opcode[0]);
  and and_1 (regdst, not_1_out, not_2_out, not_3_out);
  and and_2 (and_2_out, not_2_out, not_3_out);
  and and_3 (and_3_out, opcode[5], not_1_out);
  and and_4 (jump, opcode[1], not_4_out);
  and and_5 (bne, not_3_out, opcode[0]);
  and and_6 (beq, opcode[2], not_4_out);
  or or_1 (alusrc, opcode[3], opcode[5]);
  and and_7 (memToReg, opcode[5], not_1_out);
  and and_8 (memRead, opcode[5], not_1_out);
  and and_9 (memWrite, opcode[3], opcode[1]);
  and and_10 (ALU[1], not_1_out, not_2_out, not_3_out);
  or or_2 (regwrite, and_2_out, and_3_out);

  assign ALU[0] = opcode[2];
endmodule

module DebugComponent (
  input  [5:0] opCode,
  input  [5:0] funct,
  output Addi,
  output Load,
  output Store,
  output BEQ,
  output BNQ,
  output Jump,
  output None,
  output Add,
  output Sub,
  output AAnd,
  output OOr
);

  wire nonoOrR;

  debugStep1 debugstep1_1 (
    .opcode(opCode), .noneOrR(nonoOrR), .addi(Addi), .load(Load), .store(Store), .beq(BEQ), .bnq(BNQ),
    .jump(Jump));
  debugStep2 debugstep2_1 (.noneOrR(nonoOrR), .funct(funct), .none(None), .add(Add), .sub(Sub), .aand(AAnd), .oor(OOr));
endmodule

module debugStep1 (
  input  [5:0] opcode,
  output noneOrR,
  output addi,
  output load,
  output store,
  output beq,
  output bnq,
  output jump
);

  wire not_1_out, not_2_out, not_3_out, not_4_out, not_5_out, not_6_out;

  not not_1 (not_1_out, opcode[5]);
  not not_2 (not_2_out, opcode[4]);
  not not_3 (not_3_out, opcode[3]);
  not not_4 (not_4_out, opcode[2]);
  not not_5 (not_5_out, opcode[1]);
  not not_6 (not_6_out, opcode[0]);
  and and_1 (noneOrR, not_1_out, not_2_out, not_3_out, not_4_out, not_5_out, not_6_out);
  and and_2 (addi, not_1_out, not_2_out, opcode[3], not_4_out, not_5_out, not_6_out);
  and and_3 (load, opcode[5], not_2_out, not_3_out, not_4_out, opcode[1], opcode[0]);
  and and_4 (store, opcode[5], not_2_out, opcode[3], not_4_out, opcode[1], opcode[0]);
  and and_5 (beq, not_1_out, not_2_out, not_3_out, opcode[2], not_5_out, not_6_out);
  and and_6 (bnq, not_1_out, not_2_out, not_3_out, opcode[2], not_5_out, opcode[0]);
  and and_7 (jump, not_1_out, not_2_out, not_3_out, not_4_out, opcode[1], not_6_out);
endmodule

module debugStep2 (
  input  noneOrR,
  input  [5:0] funct,
  output none,
  output add,
  output sub,
  output aand,
  output oor
);

  wire not_1_out, not_2_out, not_3_out, not_4_out, not_5_out, not_6_out;

  not not_1 (not_1_out, funct[5]);
  not not_2 (not_2_out, funct[4]);
  not not_3 (not_3_out, funct[3]);
  not not_4 (not_4_out, funct[2]);
  not not_5 (not_5_out, funct[1]);
  not not_6 (not_6_out, funct[0]);
  and and_1 (none, noneOrR, not_1_out, not_2_out, not_3_out, not_4_out, not_5_out, not_6_out);
  and and_2 (add, noneOrR, funct[5], not_2_out, not_3_out, not_4_out, not_5_out, not_6_out);
  and and_3 (sub, noneOrR, funct[5], not_2_out, not_3_out, not_4_out, funct[1], not_6_out);
  and and_4 (aand, noneOrR, funct[5], not_2_out, not_3_out, funct[2], not_5_out, not_6_out);
  and and_5 (oor, noneOrR, funct[5], not_2_out, not_3_out, funct[2], not_5_out, funct[0]);
endmodule

module UCALU (
  input  [1:0] ALUOP,
  input  [5:0] FUNC,
  output [1:0] OUTPUT
);

  wire and_1_out, and_2_out, and_3_out, and_4_out, not_1_out, not_2_out, not_3_out, not_4_out, not_5_out,
       not_6_out, not_7_out;

  not not_1 (not_1_out, ALUOP[1]);
  not not_2 (not_2_out, ALUOP[0]);
  not not_3 (not_3_out, FUNC[4]);
  not not_4 (not_4_out, FUNC[3]);
  not not_5 (not_5_out, FUNC[2]);
  not not_6 (not_6_out, FUNC[1]);
  not not_7 (not_7_out, FUNC[0]);
  or or_1 (OUTPUT[1], not_1_out, and_1_out);
  and and_1 (and_1_out, not_2_out, FUNC[5], not_3_out, not_4_out, not_5_out, not_7_out);
  and and_2 (and_2_out, ALUOP[1], not_2_out, FUNC[5], not_3_out, not_4_out, not_5_out, FUNC[1], not_7_out);
  and and_3 (and_3_out, ALUOP[1], not_2_out, FUNC[5], not_3_out, not_4_out, FUNC[2], not_6_out, FUNC[0]);
  or or_2 (OUTPUT[0], and_2_out, and_3_out, and_4_out);
  and and_4 (and_4_out, not_1_out, ALUOP[0]);
endmodule

module UR (
  input  [31:0] BUSW,
  input  RESET,
  input  [4:0] RS,
  input  CLK,
  input  [4:0] RT,
  input  [4:0] RW,
  input  REGWRITE,
  output [31:0] RA,
  output [31:0] RB
);

  wire EnaT0, EnaT1, EnaT2, EnaT3, EnaT4, EnaT5, EnaT6, EnaT7, EnaT8, EnaT9, EnaT10, EnaT11, EnaT12, EnaT13,
       EnaT14, EnaT15, EnaT16, EnaT17, EnaT18, EnaT19, EnaT20, EnaT21, EnaT22, EnaT23, EnaT24;
  wire [31:0] DT24, R8, R9, R10, R11, R12, R13, R14, R15, R16, R17, R18, R19, R20, R21, R22, R23, R24, R25,
       R26, R27, R28, R29, R30, R31;

  Demultiplexer #(.select(5)) demultiplexer_1 (
    .out8(EnaT0), .out9(EnaT1), .out10(EnaT2), .out11(EnaT3), .out12(EnaT4), .out13(EnaT5), .out14(EnaT6),
    .out15(EnaT7), .out16(EnaT8), .out17(EnaT9), .out18(EnaT10), .out19(EnaT11), .out20(EnaT12),
    .out21(EnaT13), .out22(EnaT14), .out23(EnaT15), .out24(EnaT16), .out25(EnaT17), .out26(EnaT18),
    .out27(EnaT19), .out28(EnaT20), .out29(EnaT21), .out30(EnaT22), .out31(EnaT23), .in(REGWRITE), .sel(RW));  // open: out0, out1, out2, out3, out4, out5, out6, out7
  Register #(.width(32)) t0 (.D(BUSW), .en(EnaT0), .Q(R8), .clk(CLK), .clr(RESET));
  Register #(.width(32)) t1 (.D(BUSW), .en(EnaT1), .Q(R9), .clk(CLK), .clr(RESET));
  Register #(.width(32)) t2 (.D(BUSW), .en(EnaT2), .Q(R10), .clk(CLK), .clr(RESET));
  Register #(.width(32)) t3 (.D(BUSW), .en(EnaT3), .Q(R11), .clk(CLK), .clr(RESET));
  Register #(.width(32)) t4 (.D(BUSW), .en(EnaT4), .Q(R12), .clk(CLK), .clr(RESET));
  Register #(.width(32)) t5 (.D(BUSW), .en(EnaT5), .Q(R13), .clk(CLK), .clr(RESET));
  Register #(.width(32)) t6 (.D(BUSW), .en(EnaT6), .Q(R14), .clk(CLK), .clr(RESET));
  Register #(.width(32)) t7 (.D(BUSW), .en(EnaT7), .Q(R15), .clk(CLK), .clr(RESET));
  Register #(.width(32)) t8 (.D(BUSW), .en(EnaT8), .Q(R16), .clk(CLK), .clr(RESET));
  Register #(.width(32)) t9 (.D(BUSW), .en(EnaT9), .Q(R17), .clk(CLK), .clr(RESET));
  Register #(.width(32)) t10 (.D(BUSW), .en(EnaT10), .Q(R18), .clk(CLK), .clr(RESET));
  Register #(.width(32)) t11 (.D(BUSW), .en(EnaT11), .Q(R19), .clk(CLK), .clr(RESET));
  Register #(.width(32)) t12 (.D(BUSW), .en(EnaT12), .Q(R20), .clk(CLK), .clr(RESET));
  Register #(.width(32)) t13 (.D(BUSW), .en(EnaT13), .Q(R21), .clk(CLK), .clr(RESET));
  Register #(.width(32)) t14 (.D(BUSW), .en(EnaT14), .Q(R22), .clk(CLK), .clr(RESET));
  Register #(.width(32)) t15 (.D(BUSW), .en(EnaT15), .Q(R23), .clk(CLK), .clr(RESET));
  Register #(.width(32)) t16 (.D(BUSW), .en(EnaT16), .Q(R24), .clk(CLK), .clr(RESET));
  Register #(.width(32)) t17 (.D(BUSW), .en(EnaT17), .Q(R25), .clk(CLK), .clr(RESET));
  Register #(.width(32)) t18 (.D(BUSW), .en(EnaT18), .Q(R25), .clk(CLK), .clr(RESET));
  Register #(.width(32)) t19 (.D(BUSW), .en(EnaT19), .Q(R26), .clk(CLK), .clr(RESET));
  Register #(.width(32)) t20 (.D(BUSW), .en(EnaT20), .Q(R27), .clk(CLK), .clr(RESET));
  Register #(.width(32)) t21 (.D(BUSW), .en(EnaT21), .Q(R28), .clk(CLK), .clr(RESET));
  Register #(.width(32)) t22 (.D(BUSW), .en(EnaT22), .Q(R28), .clk(CLK), .clr(RESET));
  Register #(.width(32)) t23 (.D(BUSW), .en(EnaT23), .Q(R28), .clk(CLK), .clr(RESET));
  Register #(.width(32)) t24 (.D(DT24), .en(EnaT24), .Q(R29), .clk(CLK), .clr(RESET));
  Multiplexer #(.select(5), .width(32)) multiplexer_1 (
    .in8(R8), .in9(R9), .in10(R10), .in11(R11), .in12(R12), .in13(R13), .in14(R14), .in15(R15), .in16(R16),
    .in17(R17), .in18(R18), .in19(R19), .in20(R20), .in21(R21), .in22(R22), .in23(R23), .in24(R24),
    .in25(R25), .in26(R26), .in27(R27), .in28(R28), .in29(R29), .in30(R30), .in31(R31), .out(RA), .sel(RS));  // open: in0, in1, in2, in3, in4, in5, in6, in7
  Multiplexer #(.select(5), .width(32)) multiplexer_2 (
    .in8(R8), .in9(R9), .in10(R10), .in11(R11), .in12(R12), .in13(R13), .in14(R14), .in15(R15), .in16(R16),
    .in17(R17), .in18(R18), .in19(R19), .in20(R20), .in21(R21), .in22(R22), .in23(R23), .in24(R24),
    .in25(R25), .in26(R26), .in27(R27), .in28(R28), .in29(R29), .in30(R30), .in31(R31), .out(RB), .sel(RT));  // open: in0, in1, in2, in3, in4, in5, in6, in7

  // Other names for the same wires on the sheet: DT0[31:0] = BUSW; DT1[31:0] = BUSW; DT2[31:0] = BUSW;
  //   DT3[31:0] = BUSW; DT4[31:0] = BUSW; DT5[31:0] = BUSW; DT6[31:0] = BUSW; DT7[31:0] = BUSW; DT8[31:0] = BUSW;
  //   DT9[31:0] = BUSW; DT10[31:0] = BUSW; DT11[31:0] = BUSW; DT12[31:0] = BUSW; DT13[31:0] = BUSW; DT14[31:0] = BUSW;
  //   DT15[31:0] = BUSW; DT16[31:0] = BUSW; DT17[31:0] = BUSW; DT18[31:0] = BUSW; DT19[31:0] = BUSW;
  //   DT20[31:0] = BUSW; DT21[31:0] = BUSW; DT22[31:0] = BUSW; DT23[31:0] = BUSW; TSELECTORA[4:0] = RS;
  //   TSELECTORB[4:0] = RT; TSELECTORR[4:0] = RW
endmodule

module TSelector (
  input  [4:0] DIR,
  output [2:0] OUTPUT
);


  assign OUTPUT = DIR[2:0];
endmodule

module ALU (
  input  [1:0] ALUCTR,
  input  [31:0] BUSA,
  input  [31:0] BUSB,
  output [31:0] Data,
  output ZERO
);

  wire [31:0] ADDF, ANDF, ORF, SUBF;

  assign ANDF = BUSA & BUSB;  // AND_Gate and_1, 32 bits wide
  assign ORF = BUSA | BUSB;  // OR_Gate or_1, 32 bits wide
  Adder #(.width(32)) adder_1 (.a(BUSA), .b(BUSB), .out(ADDF));  // open: cin, cout
  Subtractor #(.width(32)) subtractor_1 (.a(BUSA), .b(BUSB), .out(SUBF));  // open: bin, bout
  Multiplexer #(.select(2), .width(32)) multiplexer_1 (
    .in0(ANDF), .in1(ORF), .in2(ADDF), .in3(SUBF), .out(Data), .sel(ALUCTR));
  Comparator #(.width(32)) comparator_1 (.a(Data), .b({32{1'b0}}), .eq(ZERO));  // open: gt, lt

  // Other names for the same wires on the sheet: A[31:0] = BUSA; ALUCTRL[1:0] = ALUCTR; B[31:0] = BUSB

  // Notes on the sheet:
  //   AND(00)
  //   OR(01)
  //   ADD(10)
  //   SUB(11)
endmodule

module Branch (
  input  [23:0] pcMasUno,
  input  [15:0] IMM,
  input  ZERO,
  input  beq,
  input  benq,
  output [23:0] outValue
);

  wire and_1_out, and_2_out, not_1_out, or_1_out;
  wire [23:0] adder_1_out, bit_extender_1_out, multiplexer_1_out, subtractor_1_out;

  assign bit_extender_1_out = {{9{IMM[14]}}, IMM[14:0]};  // Bit_Extender bit_extender_1
  Adder #(.width(24)) adder_1 (.a(pcMasUno), .b(bit_extender_1_out), .out(adder_1_out));  // open: cin, cout
  Subtractor #(.width(24)) subtractor_1 (
    .a(pcMasUno), .b(bit_extender_1_out), .out(subtractor_1_out));  // open: bin, bout
  Multiplexer #(.width(24)) multiplexer_1 (
    .in0(adder_1_out), .in1(subtractor_1_out), .out(multiplexer_1_out), .sel(IMM[15]));
  or or_1 (or_1_out, and_1_out, and_2_out);
  and and_1 (and_1_out, ZERO, beq);
  not not_1 (not_1_out, ZERO);
  Multiplexer #(.width(24)) multiplexer_2 (.in0(pcMasUno), .in1(multiplexer_1_out), .out(outValue), .sel(or_1_out));
  and and_2 (and_2_out, not_1_out, benq);
endmodule
